// Logisim project CircuitosCombinatorios.circ as structural Verilog: 1 circuit, main circuit main
module main (
  input  e3,
  input  e2,
  input  A,
  input  e1,
  input  A_2,
  input  B,
  input  e0,
  input  B_2,
  input  C,
  input  in_10,
  input  A_3,
  input  in_12,
  input  B_3,
  input  in_14,
  input  A_4,
  input  in_16,
  input  B_4,
  input  A_5,
  input  B_5,
  input  Ci,
  input  A_6,
  input  B_6,
  input  C_2,
  input  D,
  input  A_7,
  input  B_7,
  input  C_3,
  input  D_2,
  output s3,
  output Suma,
  output s2,
  output s1,
  output Carry,
  output s0,
  output out_35,
  output suma_2,
  output out_37,
  output carry_2,
  output out_39,
  output out_40,
  output Suma_3,
  output Co
);

  wire adder_2_cout, adder_3_cout, adder_4_cout, adder_5_cout, adder_6_cout, adder_7_cout, adder_8_cout,
       and_1_out, and_2_out, and_3_out, and_4_out, and_5_out, and_6_out, and_7_out, and_8_out, and_9_out,
       and_10_out, and_11_out, and_13_out, and_14_out, and_16_out, and_17_out, nand_1_out, nand_2_out,
       nor_1_out, nor_2_out, nor_3_out, nor_4_out, not_1_out, not_2_out, not_3_out, not_4_out, not_5_out,
       not_6_out, not_7_out, not_8_out, not_9_out, not_10_out, not_11_out, not_12_out, not_13_out,
       not_14_out, not_15_out, not_16_out, not_17_out, not_18_out, not_19_out, not_20_out, not_21_out,
       not_22_out, or_1_out, or_2_out, or_3_out, or_4_out, or_5_out, xor_1_out, xor_3_out;

  not not_1 (not_1_out, D);
  not not_2 (not_2_out, A_2);
  not not_3 (not_3_out, B_2);
  not not_4 (not_4_out, C);
  not not_5 (not_5_out, B_4);
  not not_6 (not_6_out, A_7);
  not not_7 (not_7_out, D_2);
  not not_8 (not_8_out, B_7);
  not not_9 (not_9_out, D_2);
  not not_10 (not_10_out, C_3);
  not not_11 (not_11_out, D_2);
  nor nor_1 (nor_1_out, not_2_out, not_3_out);
  and and_1 (and_1_out, A_4, B_4);
  and and_2 (and_2_out, A_4, not_5_out);
  nor nor_2 (nor_2_out, C_2, D);
  or or_1 (or_1_out, B_6, A_6);
  nand nand_1 (nand_1_out, A_6, B_6);
  and and_3 (and_3_out, not_1_out, B_6);
  and and_4 (and_4_out, D_2, not_6_out);
  and and_5 (and_5_out, A_7, not_7_out);
  and and_6 (and_6_out, D_2, not_8_out);
  and and_7 (and_7_out, B_7, not_9_out);
  and and_8 (and_8_out, D_2, not_10_out);
  and and_9 (and_9_out, C_3, not_11_out);
  not not_12 (not_12_out, nor_1_out);
  nor nor_3 (nor_3_out, and_1_out, and_2_out);
  nand nand_2 (nand_2_out, nand_1_out, C_2);
  or or_2 (or_2_out, and_4_out, and_5_out);
  or or_3 (or_3_out, and_6_out, and_7_out);
  or or_4 (or_4_out, and_8_out, and_9_out);
  nor nor_4 (nor_4_out, not_12_out, not_4_out);
  LED led_1 (.in(nor_4_out));
  and and_10 (and_10_out, nor_3_out, not_5_out);
  LED led_2 (.in(and_10_out));
  xor xor_1 (xor_1_out, nor_2_out, or_1_out);
  or or_5 (or_5_out, nand_2_out, and_3_out);
  and and_11 (and_11_out, xor_1_out, or_5_out);
  LED led_3 (.in(and_11_out));
  not not_13 (not_13_out, A);
  not not_14 (not_14_out, B);
  xor xor_2 (suma_2, A_3, B_3);
  and and_12 (carry_2, A_3, B_3);
  xor xor_3 (xor_3_out, A_5, B_5);
  and and_13 (and_13_out, not_13_out, B);
  and and_14 (and_14_out, A, not_14_out);
  and and_15 (Carry, A, B);
  xor xor_4 (Suma_3, xor_3_out, Ci);
  and and_16 (and_16_out, xor_3_out, Ci);
  and and_17 (and_17_out, A_5, B_5);
  or or_6 (Suma, and_13_out, and_14_out);
  or or_7 (Co, and_16_out, and_17_out);
  not not_15 (not_15_out, e3);
  Adder #(.width(1)) adder_1 (.a(not_15_out), .b(adder_3_cout), .out(s3));  // open: cin, cout
  not not_16 (not_16_out, e2);
  not not_17 (not_17_out, in_10);
  Adder #(.width(1)) adder_2 (.a(not_17_out), .b(adder_4_cout), .out(out_35), .cout(adder_2_cout));  // open: cin
  not not_18 (not_18_out, in_12);
  Adder #(.width(1)) adder_3 (.a(not_16_out), .b(adder_5_cout), .out(s2), .cout(adder_3_cout));  // open: cin
  not not_19 (not_19_out, e1);
  Adder #(.width(1)) adder_4 (.a(not_18_out), .b(adder_7_cout), .out(out_37), .cout(adder_4_cout));  // open: cin
  not not_20 (not_20_out, in_14);
  Adder #(.width(1)) adder_5 (.a(not_19_out), .b(adder_6_cout), .out(s1), .cout(adder_5_cout));  // open: cin
  not not_21 (not_21_out, e0);
  Adder #(.width(1)) adder_6 (.a(not_21_out), .b(1'b1), .out(s0), .cout(adder_6_cout));  // open: cin
  Adder #(.width(1)) adder_7 (.a(not_20_out), .b(adder_8_cout), .out(out_39), .cout(adder_7_cout));  // open: cin
  not not_22 (not_22_out, in_16);
  Adder #(.width(1)) adder_8 (.a(not_22_out), .b(1'b1), .out(out_40), .cout(adder_8_cout));  // open: cin
  LED led_4 (.in(adder_2_cout));

  // Notes on the sheet:
  //   SUMADOR UN BIT
  //   SUMADOR UN BIT REDUCIDO
  //   SUMADOR 2 BIT COMPLETO
  //   INVERSO ADITIVO DE UN COMPLEMENTO A 2
  //   INVERSO ADITIVO DE UN COMPLEMENTO A 2
  //   con indicador de overflow
endmodule
