// Logisim project CircuitosSecuenciales.circ as structural Verilog
module registroSimple (
  input  i0,
  input  i1,
  input  i2,
  input  i3,
  input  load,
  output o0,
  output o1,
  output o2,
  output o3
);

  wire and_1_out, clk_out;

  Clock clk (.out(clk_out));
  and and_1 (and_1_out, load, clk_out);
  D_Flip_Flop d_ff_1 (.D(i0), .clk(and_1_out), .Q(o0));  // open: Qn, preset, reset
  D_Flip_Flop d_ff_2 (.D(i1), .clk(and_1_out), .Q(o1));  // open: Qn, preset, reset
  D_Flip_Flop d_ff_3 (.D(i2), .clk(and_1_out), .Q(o2));  // open: Qn, preset, reset
  D_Flip_Flop d_ff_4 (.D(i3), .clk(and_1_out), .Q(o3));  // open: Qn, preset, reset
endmodule

module registroBidireccional (
  input  i0,
  input  i1,
  input  i2,
  input  i3,
  input  load,
  input  clk,
  input  read,
  output d0,
  output d1,
  output d2,
  output d3
);

  wire and_1_out, and_2_out, d_ff_1_q, d_ff_2_q, d_ff_3_q, d_ff_4_q, not_1_out;

  D_Flip_Flop d_ff_1 (.D(i0), .clk(and_1_out), .Q(d_ff_1_q));  // open: Qn, preset, reset
  D_Flip_Flop d_ff_2 (.D(i1), .clk(and_1_out), .Q(d_ff_2_q));  // open: Qn, preset, reset
  D_Flip_Flop d_ff_3 (.D(i2), .clk(and_1_out), .Q(d_ff_3_q));  // open: Qn, preset, reset
  D_Flip_Flop d_ff_4 (.D(i3), .clk(and_1_out), .Q(d_ff_4_q));  // open: Qn, preset, reset
  not not_1 (not_1_out, load);
  and and_1 (and_1_out, load, clk);
  assign d0 = and_2_out ? d_ff_1_q : 1'bz;  // Controlled_Buffer controlled_buffer_1
  assign d1 = and_2_out ? d_ff_2_q : 1'bz;  // Controlled_Buffer controlled_buffer_2
  assign d2 = and_2_out ? d_ff_3_q : 1'bz;  // Controlled_Buffer controlled_buffer_3
  assign d3 = and_2_out ? d_ff_4_q : 1'bz;  // Controlled_Buffer controlled_buffer_4
  and and_2 (and_2_out, not_1_out, read);
endmodule

module ExtensorDeSigno (
  input  i0,
  input  i1,
  input  i2,
  input  i3,
  input  load,
  input  ext,
  output d0,
  output d1,
  output d2,
  output d3,
  output [3:0] out_11
);

  wire and_1_out, clk_out, d_ff_1_q, d_ff_2_q, d_ff_3_q, d_ff_4_q, not_1_out;

  Clock clk (.out(clk_out));
  D_Flip_Flop d_ff_1 (.D(i0), .clk(and_1_out), .Q(d_ff_1_q));  // open: Qn, preset, reset
  D_Flip_Flop d_ff_2 (.D(i1), .clk(and_1_out), .Q(d_ff_2_q));  // open: Qn, preset, reset
  D_Flip_Flop d_ff_3 (.D(i2), .clk(and_1_out), .Q(d_ff_3_q));  // open: Qn, preset, reset
  D_Flip_Flop d_ff_4 (.D(i3), .clk(and_1_out), .Q(d_ff_4_q));  // open: Qn, preset, reset
  and and_1 (and_1_out, load, clk_out);
  assign d0 = not_1_out ? d_ff_1_q : 1'bz;  // Controlled_Buffer controlled_buffer_1
  assign d1 = not_1_out ? d_ff_2_q : 1'bz;  // Controlled_Buffer controlled_buffer_2
  assign d2 = not_1_out ? d_ff_3_q : 1'bz;  // Controlled_Buffer controlled_buffer_3
  assign d3 = not_1_out ? d_ff_4_q : 1'bz;  // Controlled_Buffer controlled_buffer_4
  not not_1 (not_1_out, ext);
  assign out_11[3] = ext ? d_ff_3_q : 1'bz;  // Controlled_Buffer controlled_buffer_5
  assign out_11[0] = ext ? d_ff_4_q : 1'bz;  // Controlled_Buffer controlled_buffer_6

  assign out_11[2:1] = {2{out_11[3]}};
endmodule

module Desplazador (
  input  i0,
  input  i1,
  input  i2,
  input  i3,
  input  load,
  input  ext,
  output d0,
  output d1,
  output d2,
  output d3,
  output [3:0] out_11
);

  wire and_1_out, clk_out, d_ff_1_q, d_ff_2_q, d_ff_3_q, d_ff_4_q, not_1_out;

  Clock clk (.out(clk_out));
  D_Flip_Flop d_ff_1 (.D(i0), .clk(and_1_out), .Q(d_ff_1_q));  // open: Qn, preset, reset
  D_Flip_Flop d_ff_2 (.D(i1), .clk(and_1_out), .Q(d_ff_2_q));  // open: Qn, preset, reset
  D_Flip_Flop d_ff_3 (.D(i2), .clk(and_1_out), .Q(d_ff_3_q));  // open: Qn, preset, reset
  D_Flip_Flop d_ff_4 (.D(i3), .clk(and_1_out), .Q(d_ff_4_q));  // open: Qn, preset, reset
  and and_1 (and_1_out, load, clk_out);
  assign d0 = not_1_out ? d_ff_1_q : 1'bz;  // Controlled_Buffer controlled_buffer_1
  assign d1 = not_1_out ? d_ff_2_q : 1'bz;  // Controlled_Buffer controlled_buffer_2
  assign d2 = not_1_out ? d_ff_3_q : 1'bz;  // Controlled_Buffer controlled_buffer_3
  assign d3 = not_1_out ? d_ff_4_q : 1'bz;  // Controlled_Buffer controlled_buffer_4
  not not_1 (not_1_out, ext);
  assign out_11[0] = ext ? d_ff_4_q : 1'bz;  // Controlled_Buffer controlled_buffer_5
  assign out_11[1] = ext ? d_ff_1_q : 1'bz;  // Controlled_Buffer controlled_buffer_6
  assign out_11[2] = ext ? d_ff_3_q : 1'bz;  // Controlled_Buffer controlled_buffer_7
  assign out_11[3] = ext ? d_ff_2_q : 1'bz;  // Controlled_Buffer controlled_buffer_8
endmodule
